# Fritzing sketch transmitter sketch (saved by Fritzing 0.9.3b)

parts:
  Part2 = Real Time Clock Module - DS1307 RTC Breakout Board
  Part3 = NRF24L01+ Breakout Board
  Part4 = Arduino Nano (Rev3.0)
  Q1 = NPN-Transistor [package="TO92 [THT]"]
  R1 = Resistor [tolerance=±5% resistance=1k package=THT]
  RHT1 = Humidity and Temperature Sensor RHT03

nets:
  5V: Part2.5V, Part4.5V, RHT1.Vcc
  GND: Part2.GND, Part3.GND, Part4.GND, RHT1.GND_1, RHT1.GND_2
  N1: Part2.SQW, Part4.D2
  N2: Part2.SCL, Part4.A5
  N3: Part2.SDA, Part4.A4
  N4: Part3.VCC, Q1.E
  N5: Part3.CE, Part4.D9
  N6: Part3.CS, Part4.D10
  N7: Part3.SCK, Part4.D13/SCK
  N8: Part3.MOSI, Part4.D11/MOSI
  N9: Part3.MISO, Part4.D12/MISO
  N10: Part4.D3, RHT1.Data-signal
  N11: Part4.D6, R1.Pin_0
  N12: Part4.3V3, Q1.C
